# Fritzing sketch Main (saved by Fritzing 0.9.6b)
breadboards: 1

parts:
  Mod1 = Raspberry Pi Pico W
  M1 = MAX7219 8x8 single Led Matrix Module
  S1 = Pushbutton [package="[THT]"]
  S2 = Pushbutton [package="[THT]"]
  S3 = Pushbutton [package="[THT]"]
  S4 = Pushbutton [package="[THT]"]
  RE1 = KY-040 Rotary encoder [package=THT]

nets:
  N1: Mod1.pin_1, RE1.CLK
  N2: Mod1.pin_2, RE1.DT
  N3: Mod1.pin_3, Mod1.pin_23, Mod1.pin_33, Mod1.pin_38, Mod1.pin_42, M1.O-GND, S1.Pin_1, S1.Pin_2, S2.Pin_1, S2.Pin_2, S3.Pin_1, S3.Pin_2, S4.Pin_1, S4.Pin_2, RE1.GND
  N4: Mod1.pin_4, RE1.SW
  N5: Mod1.pin_21, M1.I-CS, M1.O-CS
  N6: Mod1.pin_24, M1.O-CLK
  N7: Mod1.pin_25, M1.O-DOUT
  N8: Mod1.pin_31, S1.Pin_3, S1.Pin_4
  N9: Mod1.pin_32, S2.Pin_3, S2.Pin_4
  N10: Mod1.pin_36, RE1.Vcc
  N11: Mod1.pin_40, M1.O-VCC
  N12: S3.Pin_3, S3.Pin_4
  N13: S4.Pin_3, S4.Pin_4

custom parts:
  Raspberry Pi Pico W: Raspberry Pi Pico W. Based around the RP2040 microcontroller the Pico W is a low cost microcontroller device bringing Raspberry Pi quality, cost, and easy of use to the microcontroller space. The areas marked KEEPOUT in pcb silkscreen should not have traces running through them to avoid shorts on a soldered in module!
  MAX7219 8x8 single Led Matrix Module: Description: MAX7219 8x8 LedMatrix single Red Module Dimensions: 32x32mm Documents:
  KY-040 Rotary encoder: KY-040 Rotary Encoder with switch on breakout borad from AZ Delivery
