# Fritzing sketch slave (saved by Fritzing 0.9.6b)
breadboards: 2

parts:
  Mod1 = Raspberry Pi Pico W
  M1 = MAX7219 8x8 single Led Matrix Module
  S1 = Pushbutton [package="[SMD]"]
  S2 = Pushbutton [package="[SMD]"]
  S3 = Pushbutton [package="[SMD]"]
  LED2 = smd LED [color="Green (570nm)" package="0603 [SMD]"]
  LED3 = smd LED [color="Red (633nm)" package="0603 [SMD]"]
  LED4 = smd LED [color="Yellow (592nm)" package="0603 [SMD]"]
  R1 = Resistor [tolerance=±5% power=0.25 resistance=220 package=THT]
  R2 = Resistor [tolerance=±5% power=0.25 resistance=220 package=THT]
  R3 = Resistor [tolerance=±5% resistance=220 package="1206 [SMD]"]
  S4 = Pushbutton [package="[THT]"]
  LED5 = smd LED [color="Red (633nm)" package="1206 [SMD]"]
  R4 = Resistor [tolerance=±5% power=0.25 resistance=220 package=THT]
  Keypad4x1 = Keypad Membran 4x4
  U1 = POT [package=pot_mammoth]
  A1 = MAX2870 rf signal generator

nets:
  N1: Mod1.pin_1, Keypad4x1.Pin1
  N2: Mod1.pin_2, Keypad4x1.Pin2
  N3: Mod1.pin_4, Keypad4x1.Pin3
  N4: Mod1.pin_5, Keypad4x1.Pin4
  N5: Mod1.pin_6, Keypad4x1.Pin5
  N6: Mod1.pin_7, Keypad4x1.Pin6
  N7: Mod1.pin_9, Keypad4x1.Pin7
  N8: Mod1.pin_10, Keypad4x1.Pin8
  N9: Mod1.pin_11, S1.Pin_3, S1.Pin_4
  N10: Mod1.pin_12, S2.Pin_3, S2.Pin_4
  N11: Mod1.pin_14, S3.Pin_3, S3.Pin_4
  N12: Mod1.pin_15, LED3.anode, R1.Pin_0, R1.Pin_1
  N13: Mod1.pin_16, LED2.anode, R2.Pin_0, R2.Pin_1
  N14: Mod1.pin_17, LED4.anode, R3.Pin_0, R3.Pin_1
  N15: Mod1.pin_18, Mod1.pin_22, Mod1.pin_23, Mod1.pin_26, Mod1.pin_27, Mod1.pin_28, Mod1.pin_29, Mod1.pin_31, Mod1.pin_33, Mod1.pin_38, Mod1.pin_42, M1.I-GND, M1.O-GND, S1.Pin_1, S1.Pin_2, S2.Pin_1, S2.Pin_2, S3.Pin_1, S3.Pin_2, LED2.cathode, LED3.cathode, LED4.cathode, S4.Pin_1, S4.Pin_2, LED5.cathode, U1.E
  N16: Mod1.pin_19, LED5.anode, R4.Pin_0, R4.Pin_1
  N17: Mod1.pin_20, S4.Pin_4
  N18: Mod1.pin_21, M1.I-CS, M1.O-CS
  N19: Mod1.pin_24, M1.I-CLK, M1.O-CLK
  N20: Mod1.pin_25, M1.I-DIN
  N21: Mod1.pin_32, A1.Pin_3
  N22: Mod1.pin_34, U1.A
  N23: Mod1.pin_36, U1.S
  N24: Mod1.pin_40, M1.I-VCC, M1.O-VCC

custom parts:
  Raspberry Pi Pico W: Raspberry Pi Pico W. Based around the RP2040 microcontroller the Pico W is a low cost microcontroller device bringing Raspberry Pi quality, cost, and easy of use to the microcontroller space. The areas marked KEEPOUT in pcb silkscreen should not have traces running through them to avoid shorts on a soldered in module!
  MAX7219 8x8 single Led Matrix Module: Description: MAX7219 8x8 LedMatrix single Red Module Dimensions: 32x32mm Documents:
  Keypad Membran 4x4: Membrane Keypad 4x4 Matrix
  MAX2870 rf signal generator: MAX2870 rf signal generator.
